# Fritzing sketch seq (saved by Fritzing 0.9.2b)

parts:
  Part1 = Arduino Uno (Rev3)
  Part2 = EasyDriver_v44
  Part3 = Color Sensor Breakout ADJD-S311
  M1 = Stepper Motor - Bipolar

nets:
  N1: Part1.A4/SDA, Part3.SDA
  N2: Part1.A5/SCL, Part3.SCL
  GND: Part1.GND, Part2.GND, Part3.GND
  N3: Part1.D2, Part2.STEP
  N4: Part1.D3_PWM, Part2.DIR
  N5: Part1.D4, Part2.MS1
  N6: Part1.D5_PWM, Part2.MS2
  N7: Part1.D6_PWM, Part2.ENABLE
  N8: Part1.D7, Part3.LED
  3V3: Part1.3V3, Part3.VCC
  N9: Part2.OUT2A, M1.A
  N10: Part2.OUT2B, M1.B
  N11: Part2.OUT1A, M1.C
  N12: Part2.OUT1B, M1.D
